// Logisim project RSC.circ as structural Verilog: 9 circuits, main circuit Arith_U
// AU
module Arith_U (
  input  [31:0] A,
  input  [31:0] B,
  input  S0,
  input  S1,
  output [31:0] Au_out
);

  wire AND_out, not_2_out;
  wire [31:0] adder_1_out, multiplexer_1_out, not_1_out;

  assign not_1_out = ~B;  // NOT_Gate not_1, 32 bits wide
  Multiplexer #(.select(2), .width(32), .enable("false")) multiplexer_1 (
    .in0(not_1_out), .in1(B), .in2({32{1'b0}}), .in3(B), .out(multiplexer_1_out), .sel({S1, S0}));
  not not_2 (not_2_out, S0);
  Adder #(.width(32)) adder_1 (.a(A), .b(multiplexer_1_out), .out(adder_1_out), .cin(not_2_out));  // open: cout
  Multiplexer #(.width(32), .enable("false")) multiplexer_2 (.in0(adder_1_out), .in1(B), .out(Au_out), .sel(AND_out));
  and AND (AND_out, S1, S0);
endmodule

// LU
module Logic_U (
  input  [31:0] A,
  input  S1,
  input  S0,
  input  [31:0] B,
  output [31:0] Logic_out
);

  wire [31:0] and_1_out, not_1_out, or_1_out, shifter_1_out;

  assign and_1_out = A & B;  // AND_Gate and_1, 32 bits wide
  assign or_1_out = A | B;  // OR_Gate or_1, 32 bits wide
  Shifter #(.width(32), .shift("ar")) shifter_1 (.in(A), .\dist (5'b00001), .out(shifter_1_out));
  assign not_1_out = ~A;  // NOT_Gate not_1, 32 bits wide
  Multiplexer #(.select(2), .width(32), .enable("false")) multiplexer_1 (
    .in0(and_1_out), .in1(or_1_out), .in2(shifter_1_out), .in3(not_1_out), .out(Logic_out), .sel({S1, S0}));
endmodule

module ALU (
  input  [31:0] A,
  input  [31:0] B,
  input  S2,
  input  S1,
  input  S0,
  output [31:0] ALU_Out
);

  wire [31:0] arith_u_1_au_out, logic_u_1_logic_out;

  Arith_U arith_u_1 (.A(A), .B(B), .S1(S1), .S0(S0), .Au_out(arith_u_1_au_out));
  Logic_U logic_u_1 (.A(A), .B(B), .S1(S1), .S0(S0), .Logic_out(logic_u_1_logic_out));
  Multiplexer #(.width(32), .enable("false")) multiplexer_1 (
    .in0(arith_u_1_au_out), .in1(logic_u_1_logic_out), .out(ALU_Out), .sel(S2));
endmodule

module SC (
  input  Clock,
  input  Clear,
  output [2:0] SEQ_out
);

  wire [2:0] adder_1_out;

  Adder #(.width(3)) adder_1 (.a(SEQ_out), .b(3'b001), .out(adder_1_out));  // open: cin, cout
  Register #(.width(3)) register_1 (.D(adder_1_out), .Q(SEQ_out), .clk(Clock), .clr(Clear));  // open: en
endmodule

module RSC (
  output [31:0] PC_OUT,
  output [31:0] DR_OUT,
  output [31:0] IR_OUT,
  output [7:0] T,
  output [3:0] D,
  output [31:0] R_OUT,
  output [31:0] ACC_OUT
);

  wire control_1_acc_bus, control_1_acc_clr, control_1_acc_ld, control_1_ar_ld, control_1_dr_bus,
       control_1_dr_ld, control_1_ir_ld, control_1_outr_ld, control_1_r_bus, control_1_r_ld,
       control_1_ram_en, control_1_ram_r_prime_w, control_1_z_ld, pc_1_p2, pc_1_p4, pc_1_p5,
       Primary_Clock_out, z_reg_1_z_out;
  wire [2:0] control_1_alu_s;
  wire [31:0] alu_1_alu_out, ar_1_data_out, outr_1_data_out, r_1_bus_out;

  Clock Primary_Clock (.out(Primary_Clock_out));
  OUTR outr_1 (.Data_In(r_1_bus_out), .Clock(Primary_Clock_out), .Load(control_1_outr_ld), .Data_out(outr_1_data_out));
  Hex_Digit_Display hex_digit_display_1 (.value(outr_1_data_out[31:28]), .dp(1'b0));
  AR ar_1 (.Data_In(r_1_bus_out), .Clock(Primary_Clock_out), .Load(control_1_ar_ld), .Data_out(ar_1_data_out));
  R r_1 (
    .Data_In(r_1_bus_out), .Clock(Primary_Clock_out), .Load(control_1_r_ld), .Bus(control_1_r_bus),
    .Data_Out(R_OUT), .Bus_out(r_1_bus_out));
  Hex_Digit_Display hex_digit_display_2 (.value(outr_1_data_out[23:20]), .dp(1'b0));
  Hex_Digit_Display hex_digit_display_3 (.value(outr_1_data_out[27:24]), .dp(1'b0));
  DR dr_1 (
    .Data_In(r_1_bus_out), .Clock(Primary_Clock_out), .Load(control_1_dr_ld), .Bus(control_1_dr_bus),
    .Data_Out(DR_OUT), .Bus_out(r_1_bus_out));
  ALU alu_1 (
    .A(ACC_OUT), .B(r_1_bus_out), .S2(control_1_alu_s[2]), .S1(control_1_alu_s[1]), .S0(control_1_alu_s[0]),
    .ALU_Out(alu_1_alu_out));
  Hex_Digit_Display hex_digit_display_4 (.value(outr_1_data_out[19:16]), .dp(1'b0));
  // PC pc_1: pin names not known; wires that end beside it: r_1_bus_out, pc_1_p2, Primary_Clock_out, pc_1_p4, pc_1_p5, PC_OUT, r_1_bus_out
  ACC acc_1 (
    .Data_In(alu_1_alu_out), .Clock(Primary_Clock_out), .Load(control_1_acc_ld), .Clear(control_1_acc_clr),
    .Bus(control_1_acc_bus), .Data_Out(ACC_OUT), .Bus_out(r_1_bus_out));
  Hex_Digit_Display hex_digit_display_5 (.value(outr_1_data_out[15:12]), .dp(1'b0));
  RAM #(.addrWidth(16), .dataWidth(32)) ram_1 (
    .addr(ar_1_data_out[15:0]), .data(r_1_bus_out), .sel(control_1_ram_en), .clk(Primary_Clock_out),
    .ld(control_1_ram_r_prime_w), .clr(1'b0));
  Hex_Digit_Display hex_digit_display_6 (.value(outr_1_data_out[11:8]), .dp(1'b0));
  Hex_Digit_Display hex_digit_display_7 (.value(outr_1_data_out[7:4]), .dp(1'b0));
  Hex_Digit_Display hex_digit_display_8 (.value(outr_1_data_out[3:0]), .dp(1'b0));
  IR ir_1 (.Data_In(DR_OUT), .Clock(Primary_Clock_out), .Load(control_1_ir_ld), .Data_out(IR_OUT));
  Z_Reg z_reg_1 (.ACC_in(ACC_OUT), .Clock(Primary_Clock_out), .Load(control_1_z_ld), .Z_out(z_reg_1_z_out));
  Control control_1 (
    .RAM_R_prime_W(control_1_ram_r_prime_w), .RAM_EN(control_1_ram_en), .AR_LD(control_1_ar_ld),
    .PC_BUS(pc_1_p5), .PC_INC(pc_1_p4), .PC_LD(pc_1_p2), .DR_BUS(control_1_dr_bus), .DR_LD(control_1_dr_ld),
    .R_BUS(control_1_r_bus), .R_LD(control_1_r_ld), .ACC_BUS(control_1_acc_bus), .ACC_CLR(control_1_acc_clr),
    .ACC_LD(control_1_acc_ld), .ALU_S(control_1_alu_s), .OUTR_LD(control_1_outr_ld), .Z_LD(control_1_z_ld),
    .IR_LD(control_1_ir_ld), .Clock(Primary_Clock_out), .Z_In(z_reg_1_z_out), .T(T), .IR_In(IR_OUT), .D(D));

  // Notes on the sheet:
  //   Jaylon Atkins
  //   OLA5
  //   RSC
endmodule

module Decoder (
  input  [31:0] IR_In,
  output [15:0] D_Out,
  output [3:0] Debug_Instruction
);

  wire or_1_out;
  wire [3:0] or_2_out;
  wire [15:0] decoder_1_out0;

  Multiplexer #(.width(16), .enable("false")) multiplexer_1 (
    .in0(decoder_1_out0), .in1({16{1'b0}}), .out(D_Out), .sel(or_1_out));
  or or_1 (or_1_out, or_2_out[3], or_2_out[2], or_2_out[1], or_2_out[0]);
  assign or_2_out = IR_In[7:4] | IR_In[11:8] | IR_In[15:12] | IR_In[19:16] | IR_In[23:20] | IR_In[27:24] | IR_In[31:28];  // OR_Gate or_2, 4 bits wide
  Decoder_part #(.select(4), .enable("false")) decoder_1 (
    .out0(decoder_1_out0[0]), .out1(decoder_1_out0[1]), .out2(decoder_1_out0[2]), .out3(decoder_1_out0[3]),
    .out4(decoder_1_out0[4]), .out5(decoder_1_out0[5]), .out6(decoder_1_out0[6]), .out7(decoder_1_out0[7]),
    .out8(decoder_1_out0[8]), .out9(decoder_1_out0[9]), .out10(decoder_1_out0[10]),
    .out11(decoder_1_out0[11]), .out12(decoder_1_out0[12]), .out13(decoder_1_out0[13]),
    .out14(decoder_1_out0[14]), .out15(decoder_1_out0[15]), .sel(IR_In[3:0]));

  assign Debug_Instruction = IR_In[3:0];

  // Notes on the sheet:
  //   Jaylon Atkins
  //   Decoder
  //   CLA 8
endmodule

// T
module Timer (
  input  Clock,
  input  Clear,
  input  Stop,
  output [7:0] T_Out
);

  wire [2:0] sc_1_seq_out;
  wire [7:0] decoder_1_out0;

  Multiplexer #(.width(8), .enable("false")) multiplexer_1 (
    .in0(decoder_1_out0), .in1({8{1'b0}}), .out(T_Out), .sel(Stop));
  Decoder_part #(.select(3), .enable("false")) decoder_1 (
    .out0(decoder_1_out0[0]), .out1(decoder_1_out0[1]), .out2(decoder_1_out0[2]), .out3(decoder_1_out0[3]),
    .out4(decoder_1_out0[4]), .out5(decoder_1_out0[5]), .out6(decoder_1_out0[6]), .out7(decoder_1_out0[7]),
    .sel(sc_1_seq_out));
  SC sc_1 (.Clear(Clear), .Clock(Clock), .SEQ_out(sc_1_seq_out));

  // Notes on the sheet:
  //   Jaylon Atkins
  //   Timer
  //   CLA 8
endmodule

// Z
module Z_Reg (
  input  Clock,
  input  [31:0] ACC_in,
  input  Load,
  output Z_out
);

  wire not_1_out, or_2_out;
  wire [3:0] or_1_out;

  assign or_1_out = ACC_in[3:0] | ACC_in[7:4] | ACC_in[11:8] | ACC_in[15:12] | ACC_in[19:16] | ACC_in[23:20] | ACC_in[27:24] | ACC_in[31:28];  // OR_Gate or_1, 4 bits wide
  or or_2 (or_2_out, or_1_out[0], or_1_out[1], or_1_out[2], or_1_out[3]);
  not not_1 (not_1_out, or_2_out);
  _1bit_reg u_1bit_reg_1 (.Data(not_1_out), .Clock(Clock), .Load(Load), .Clear(1'b0), .Data_out(Z_out));

  // Notes on the sheet:
  //   Jaylon Atkins
  //   Timer
  //   OLA 7
endmodule

module Control (
  input  Clock,
  input  [31:0] IR_In,
  input  Z_In,
  output IR_LD,
  output RAM_R_prime_W,
  output [7:0] T,
  output RAM_EN,
  output AR_LD,
  output [3:0] D,
  output PC_BUS,
  output PC_INC,
  output PC_LD,
  output DR_BUS,
  output DR_LD,
  output R_BUS,
  output R_LD,
  output ACC_BUS,
  output ACC_CLR,
  output ACC_LD,
  output [2:0] ALU_S,
  output OUTR_LD,
  output Z_LD
);

  wire n1bit_reg_1_data_out, s_ld_1_p4, sc_clr_1_sc_clr;
  wire [15:0] s_ld_1_p2;

  RAM_RW ram_rw_1 (
    .t1(T[1]), .t3(T[3]), .t5(T[5]), .d1(s_ld_1_p2[1]), .d2(s_ld_1_p2[2]), .d5(s_ld_1_p2[5]),
    .d6(s_ld_1_p2[6]), .z(Z_In), .RAM_RW(RAM_R_prime_W));
  RAM_EN ram_en_1 (
    .t1(T[1]), .t3(T[3]), .t5(T[5]), .t6(T[6]), .d1(s_ld_1_p2[1]), .d2(s_ld_1_p2[2]), .d5(s_ld_1_p2[5]),
    .d6(s_ld_1_p2[6]), .z(Z_In), .RAM_EN(RAM_EN));
  AR_LD ar_ld_1 (.t0(T[0]), .t2(T[2]), .t4(T[4]), .clock(Clock), .d1(s_ld_1_p2[1]), .d2(s_ld_1_p2[2]), .AR_LD(AR_LD));
  PC_BUS pc_bus_1 (.t0(T[0]), .t2(T[2]), .PC_BUS(PC_BUS));
  PC_INC pc_inc_1 (
    .t1(T[1]), .t3(T[3]), .clock(Clock), .d1(s_ld_1_p2[1]), .d2(s_ld_1_p2[2]), .d6(s_ld_1_p2[6]), .z(Z_In),
    .PC_INC(PC_INC));
  PC_LD pc_ld_1 (.t4(T[4]), .clock(Clock), .d5(s_ld_1_p2[5]), .d6(s_ld_1_p2[6]), .z(Z_In), .PC_LD(PC_LD));
  DR_BUS dr_bus_1 (
    .t4(T[4]), .t6(T[6]), .d1(s_ld_1_p2[1]), .d2(s_ld_1_p2[2]), .d5(s_ld_1_p2[5]), .d6(s_ld_1_p2[6]),
    .z(Z_In), .DR_BUS(DR_BUS));
  DR_LD dr_ld_1 (
    .t1(T[1]), .t3(T[3]), .t5(T[5]), .clock(Clock), .d1(s_ld_1_p2[1]), .d2(s_ld_1_p2[2]), .d5(s_ld_1_p2[5]),
    .d6(s_ld_1_p2[6]), .z(Z_In), .DR_LD(DR_LD));
  R_BUS r_bus_1 (
    .t3(T[3]), .d4(s_ld_1_p2[4]), .d8(s_ld_1_p2[8]), .d9(s_ld_1_p2[9]), .d12(s_ld_1_p2[12]),
    .d13(s_ld_1_p2[13]), .R_BUS(R_BUS));
  // R_LD r_ld_1: pin names not known; wires that end beside it: R_LD, Clock, s_ld_1_p2[3], T[3]
  ACC_BUS acc_bus_1 (.t3(T[3]), .t5(T[5]), .d2(s_ld_1_p2[2]), .d3(s_ld_1_p2[3]), .d7(s_ld_1_p2[7]), .ACC_BUS(ACC_BUS));
  ACC_CLR acc_clr_1 (.t3(T[3]), .d11(s_ld_1_p2[11]), .ACC_CLR(ACC_CLR));
  ACC_LD acc_ld_1 (
    .t3(T[3]), .t6(T[6]), .clock(Clock), .d1(s_ld_1_p2[1]), .d4(s_ld_1_p2[4]), .d8(s_ld_1_p2[8]),
    .d9(s_ld_1_p2[9]), .d10(s_ld_1_p2[10]), .d12(s_ld_1_p2[12]), .d13(s_ld_1_p2[13]), .d14(s_ld_1_p2[14]),
    .d15(s_ld_1_p2[15]), .ACC_LD(ACC_LD));
  ALU_SEL alu_sel_1 (
    .d1(s_ld_1_p2[1]), .d4(s_ld_1_p2[4]), .d9(s_ld_1_p2[9]), .d10(s_ld_1_p2[10]), .d12(s_ld_1_p2[12]),
    .d13(s_ld_1_p2[13]), .d14(s_ld_1_p2[14]), .d15(s_ld_1_p2[15]), .S0(ALU_S[0]), .S1(ALU_S[1]), .S2(ALU_S[2]));
  // OUTR_LD outr_ld_1: pin names not known; wires that end beside it: OUTR_LD, Clock, s_ld_1_p2[7], T[3]
  Z_LD z_ld_1 (.Z_LD(Z_LD));
  // IR_LD ir_ld_1: pin names not known; wires that end beside it: IR_LD, Clock, T[2]
  SC_CLR sc_clr_1 (
    .t4(T[4]), .t5(T[5]), .t7(T[7]), .d1(s_ld_1_p2[1]), .d2(s_ld_1_p2[2]), .d5(s_ld_1_p2[5]),
    .d6(s_ld_1_p2[6]), .z(Z_In), .SC_CLR(sc_clr_1_sc_clr));
  // S_LD s_ld_1: pin names not known; wires that end beside it: T[3], s_ld_1_p2[0], Clock, s_ld_1_p4
  Timer timer_1 (.T_Out(T), .Clock(Clock), .Stop(n1bit_reg_1_data_out), .Clear(sc_clr_1_sc_clr));
  Decoder Decoder (.D_Out(s_ld_1_p2), .Debug_Instruction(D), .IR_In(IR_In));
  _1bit_reg u_1bit_reg_1 (.Data(1'b1), .Clock(Clock), .Load(s_ld_1_p4), .Clear(1'b0), .Data_out(n1bit_reg_1_data_out));

  // Notes on the sheet:
  //   Jaylon Atkins
  //   Control
  //   OLA 7
endmodule
