// Logisim project bin_converter.circ as structural Verilog: 2 circuits, main circuit bin_converter
module bin_converter (
  input  [2:0] ABC,
  output T,
  output U,
  output V,
  output W,
  output X,
  output Y,
  output Z
);

  wire AND_2_out, AND_3_out, AND_out, OR_2_out, OR_out;

  and AND (AND_out, ABC[2], ABC[1]);
  and AND_2 (AND_2_out, ABC[2], ABC[1]);
  and AND_3 (AND_3_out, ABC[2], ABC[2]);
  or OR (OR_out, ABC[2], ABC[1]);
  and AND_4 (U, ABC[2], ABC[1]);
  or OR_2 (OR_2_out, ABC[1], ABC[0]);
  and AND_5 (T, AND_out, ABC[0]);
  or OR_3 (Y, ABC[2], ABC[1]);
  or OR_4 (Z, OR_out, ABC[0]);
  or OR_5 (V, AND_2_out, AND_3_out);
  and AND_6 (X, OR_2_out, ABC[2]);

  assign W = ABC[2];

  // Notes on the sheet:
  //   Jaylon Atkins
  //   OLA 3
endmodule

module Display (
  input  [2:0] in_1
);

  wire bin_converter_1_p4, bin_converter_1_p5, bin_converter_1_p6, bin_converter_1_p7, bin_converter_1_p8,
       bin_converter_1_p9, bin_converter_1_p10;

  // bin_converter bin_converter_1: pin names not known; wires that end beside it: in_1[2], in_1[1], in_1[0], bin_converter_1_p4, bin_converter_1_p5, bin_converter_1_p6, bin_converter_1_p7, bin_converter_1_p8, bin_converter_1_p9, bin_converter_1_p10
  LED led_1 (.in(bin_converter_1_p4));
  LED led_2 (.in(bin_converter_1_p5));
  LED led_3 (.in(bin_converter_1_p6));
  LED led_4 (.in(bin_converter_1_p7));
  LED led_5 (.in(bin_converter_1_p8));
  LED led_6 (.in(bin_converter_1_p9));
  LED led_7 (.in(bin_converter_1_p10));
endmodule
