// Logisim project buses.circ as structural Verilog: 3 circuits, main circuit 2-bit Bus w/ 1x MUX
module _2_bit_Bus_w__mult__MUX (
  input  Clock,
  input  R0_LD,
  input  R1_LD,
  input  R2_LD,
  input  R3_LD,
  input  [1:0] R_BUS
);

  wire [1:0] multiplexer_1_out, register_1_q, register_2_q, register_3_q, register_4_q;

  Register #(.width(2)) register_1 (.D(multiplexer_1_out), .en(R0_LD), .Q(register_1_q), .clk(Clock));  // open: clr
  Register #(.width(2)) register_2 (.D(multiplexer_1_out), .en(R1_LD), .Q(register_2_q), .clk(Clock));  // open: clr
  Register #(.width(2)) register_3 (.D(multiplexer_1_out), .en(R2_LD), .Q(register_3_q), .clk(Clock));  // open: clr
  Register #(.width(2)) register_4 (.D(multiplexer_1_out), .en(R3_LD), .Q(register_4_q), .clk(Clock));  // open: clr
  // Probe on multiplexer_1_out
  Multiplexer #(.select(2), .enable("false")) multiplexer_1 (
    .in0(register_1_q[0]), .in1(register_2_q[0]), .in2(register_3_q[0]), .in3(register_4_q[0]),
    .out(multiplexer_1_out[0]), .sel(R_BUS));
  Multiplexer #(.select(2), .enable("false")) multiplexer_2 (
    .in0(register_1_q[1]), .in1(register_2_q[1]), .in2(register_3_q[1]), .in3(register_4_q[1]),
    .out(multiplexer_1_out[1]), .sel(R_BUS));

  // Notes on the sheet:
  //   2-bit Bus - 1-bit Multiplexers
  //   R0
  //   R1
  //   R2
  //   R3
endmodule

// H.A.
module _2_bit_Bus_w__1x_MUX (
  input  Clock,
  input  R1_LD,
  input  R2_LD,
  input  R3_LD,
  input  R4_LD,
  input  [1:0] R_BUS
);

  wire [1:0] multiplexer_1_out, register_1_q, register_2_q, register_3_q, register_4_q;

  Register #(.width(2)) register_1 (.D(multiplexer_1_out), .en(R1_LD), .Q(register_1_q), .clk(Clock));  // open: clr
  Register #(.width(2)) register_2 (.D(multiplexer_1_out), .en(R2_LD), .Q(register_2_q), .clk(Clock));  // open: clr
  Register #(.width(2)) register_3 (.D(multiplexer_1_out), .en(R3_LD), .Q(register_3_q), .clk(Clock));  // open: clr
  Register #(.width(2)) register_4 (.D(multiplexer_1_out), .en(R4_LD), .Q(register_4_q), .clk(Clock));  // open: clr
  // Probe on multiplexer_1_out
  Multiplexer #(.select(2), .width(2), .enable("false")) multiplexer_1 (
    .in0(register_1_q), .in1(register_2_q), .in2(register_3_q), .in3(register_4_q), .out(multiplexer_1_out),
    .sel(R_BUS));

  // Notes on the sheet:
  //   2-bit Bus - Multi-bit multiplexer
  //   R1
  //   R2
  //   R3
  //   R4
endmodule

module _4_bit_Bus_w__TSB (
  input  Clock,
  input  R0_LD,
  input  R0_BUS,
  input  R1_LD,
  input  R1_BUS,
  input  R2_LD,
  input  R2_BUS,
  input  R3_LD,
  input  R3_BUS
);

  wire [3:0] controlled_buffer_1_out, register_1_q, register_2_q, register_3_q, register_4_q;

  assign controlled_buffer_1_out = R0_BUS ? register_1_q : 4'bz;  // Controlled_Buffer controlled_buffer_1
  Register #(.width(4)) register_1 (
    .D(controlled_buffer_1_out), .en(R0_LD), .Q(register_1_q), .clk(Clock));  // open: clr
  assign controlled_buffer_1_out = R1_BUS ? register_2_q : 4'bz;  // Controlled_Buffer controlled_buffer_2
  Register #(.width(4)) register_2 (
    .D(controlled_buffer_1_out), .en(R1_LD), .Q(register_2_q), .clk(Clock));  // open: clr
  assign controlled_buffer_1_out = R2_BUS ? register_3_q : 4'bz;  // Controlled_Buffer controlled_buffer_3
  Register #(.width(4)) register_3 (
    .D(controlled_buffer_1_out), .en(R2_LD), .Q(register_3_q), .clk(Clock));  // open: clr
  Register #(.width(4)) register_4 (
    .D(controlled_buffer_1_out), .en(R3_LD), .Q(register_4_q), .clk(Clock));  // open: clr
  assign controlled_buffer_1_out = R3_BUS ? register_4_q : 4'bz;  // Controlled_Buffer controlled_buffer_4
  // Probe on controlled_buffer_1_out

  // Notes on the sheet:
  //   4-bit Bus - Tri-state Buffers
  //   R0
  //   R1
  //   R2
  //   R3
endmodule
