// Logisim project combinational.circ as structural Verilog: 18 circuits, main circuit Half Adder
// H.A.
module Half_Adder (
  input  A,
  input  B,
  output Sum,
  output Carry_Out
);

  and and_1 (Carry_Out, A, B);
  xor xor_1 (Sum, A, B);

  // Notes on the sheet:
  //   Half Adder - Add two bits
endmodule

module Full_Adder_w_o_H_A (
  input  Carry_In__C,
  input  A,
  input  B,
  output Sum,
  output Carry_Out
);

  wire and_1_out, and_2_out, xor_1_out;

  and and_1 (and_1_out, A, B);
  xor xor_1 (xor_1_out, A, B);
  and and_2 (and_2_out, Carry_In__C, xor_1_out);
  or or_1 (Carry_Out, and_1_out, and_2_out);
  xor xor_2 (Sum, Carry_In__C, xor_1_out);

  // Notes on the sheet:
  //   Full Adder (no H.A.) - Add two bits and carry-in
  //   C-out = AB + C(A⊕B)
  //   Sum = C XOR A XOR B
endmodule

// F.A.
module Full_Adder_w__H_A (
  input  Carry_In__C,
  input  A,
  input  B,
  output Sum,
  output Carry_Out
);

  wire half_adder_1_carry_out, half_adder_1_sum, half_adder_2_carry_out;

  Half_Adder half_adder_1 (.A(A), .B(B), .Sum(half_adder_1_sum), .Carry_Out(half_adder_1_carry_out));
  or or_1 (Carry_Out, half_adder_1_carry_out, half_adder_2_carry_out);
  Half_Adder half_adder_2 (.A(Carry_In__C), .B(half_adder_1_sum), .Sum(Sum), .Carry_Out(half_adder_2_carry_out));

  // Notes on the sheet:
  //   Full Adder - Two half-adders
endmodule

// 4BA
module _4_bit_Adder (
  input  Carry_In,
  input  [3:0] A,
  input  [3:0] B,
  output [3:0] Sum,
  output Carry_Out
);

  wire full_adder_w_h_a_1_carry_out, full_adder_w_h_a_2_carry_out, full_adder_w_h_a_3_carry_out;

  Full_Adder_w__H_A full_adder_w_h_a_1 (
    .A(A[0]), .B(B[0]), .Carry_In__C(Carry_In), .Carry_Out(full_adder_w_h_a_1_carry_out), .Sum(Sum[0]));
  Full_Adder_w__H_A full_adder_w_h_a_2 (
    .A(A[1]), .B(B[1]), .Carry_In__C(full_adder_w_h_a_1_carry_out), .Carry_Out(full_adder_w_h_a_2_carry_out),
    .Sum(Sum[1]));
  Full_Adder_w__H_A full_adder_w_h_a_3 (
    .A(A[2]), .B(B[2]), .Carry_In__C(full_adder_w_h_a_2_carry_out), .Carry_Out(full_adder_w_h_a_3_carry_out),
    .Sum(Sum[2]));
  Full_Adder_w__H_A full_adder_w_h_a_4 (
    .A(A[3]), .B(B[3]), .Carry_In__C(full_adder_w_h_a_3_carry_out), .Carry_Out(Carry_Out), .Sum(Sum[3]));
  Half_Adder half_adder_1 ();  // open: A, B, Sum, Carry_Out

  // Notes on the sheet:
  //   4-bit Adder - Full and Half Adders (ripple-carry adder)
endmodule

module _4_bit_Subtractor (
  input  [3:0] A,
  input  [3:0] B,
  output [3:0] Difference,
  output Borrow
);

  wire n4_bit_adder_1_carry_out;
  wire [3:0] not_1_out;

  assign not_1_out = ~B;  // NOT_Gate not_1, 4 bits wide
  _4_bit_Adder u_4_bit_adder_1 (
    .A(A), .B(not_1_out), .Carry_In(1'b1), .Carry_Out(n4_bit_adder_1_carry_out), .Sum(Difference));
  not not_2 (Borrow, n4_bit_adder_1_carry_out);

  // Notes on the sheet:
  //   4-bit Subtractor - 2's Complement Addition
  //   == 1  => (A < B)
  //   == 0  => (A >= B)
endmodule

module _8_bit_Adder (
  input  Carry_In,
  input  [7:0] A,
  input  [7:0] B,
  output [7:0] Sum,
  output Carry_Out
);

  wire n4_bit_adder_1_carry_out;

  _4_bit_Adder u_4_bit_adder_1 (
    .A(A[3:0]), .B(B[3:0]), .Carry_In(Carry_In), .Carry_Out(n4_bit_adder_1_carry_out), .Sum(Sum[3:0]));
  _4_bit_Adder u_4_bit_adder_2 (
    .A(A[7:4]), .B(B[7:4]), .Carry_In(n4_bit_adder_1_carry_out), .Carry_Out(Carry_Out), .Sum(Sum[7:4]));

  // Notes on the sheet:
  //   8-bit Adder - 2x 4-bit Adders (in class)
endmodule

module _4_bit_Shifter (
  input  [3:0] Input,
  input  S__0___L__1___R,
  output [3:0] Output
);

  wire not_1_out, S_prime_C_out, S_prime_D_out, SA_out, SB_out;

  not not_1 (not_1_out, S__0___L__1___R);
  and SA (SA_out, S__0___L__1___R, Input[3]);
  and S_prime_B (Output[3], not_1_out, Input[2]);
  and SB (SB_out, S__0___L__1___R, Input[2]);
  and S_prime_C (S_prime_C_out, not_1_out, Input[1]);
  and SC (Output[0], S__0___L__1___R, Input[1]);
  and S_prime_D (S_prime_D_out, not_1_out, Input[0]);
  or or_1 (Output[2], SA_out, S_prime_C_out);
  or or_2 (Output[1], SB_out, S_prime_D_out);

  // Notes on the sheet:
  //   4-bit Shifter - Shift one bit to the (L/R) if S == (0/1)
endmodule

module _1_bit_Comparator (
  input  A,
  input  B,
  output LT,
  output EQ,
  output GT
);

  wire not_1_out, not_2_out;

  not not_1 (not_1_out, A);
  not not_2 (not_2_out, B);
  and and_1 (LT, B, not_1_out);
  xnor xnor_1 (EQ, A, B);
  and and_2 (GT, not_2_out, A);

  // Notes on the sheet:
  //   1-bit Comparator - Output if A is LT, EQ, or GT B
endmodule

// Cmp
module _1_bit_Comparator__rev (
  input  LT,
  input  EQ,
  input  GT,
  input  X,
  input  Y,
  output LT_2,
  output EQ_2,
  output GT_2
);

  wire and_1_out, and_2_out;

  and and_1 (and_1_out, ~X, Y, EQ);  // AND_Gate
  and and_2 (and_2_out, EQ, X, ~Y);  // AND_Gate
  or or_1 (LT_2, LT, and_1_out);
  nor nor_1 (EQ_2, LT_2, GT_2);
  or or_2 (GT_2, and_2_out, GT);

  // Notes on the sheet:
  //   1-bit Comparator (rev.) - Allow cascading
endmodule

module _2_bit_Comparator__bad (
  input  [1:0] A,
  input  [1:0] B,
  output LT,
  output EQ,
  output GT
);

  wire and_1_out, and_2_out, and_3_out, and_4_out, and_5_out, and_6_out, or_1_out, or_2_out, or_5_out,
       or_6_out;

  and and_1 (and_1_out, ~A[1], B[1]);  // AND_Gate
  and and_2 (and_2_out, ~A[0], B[1], B[0]);  // AND_Gate
  and and_3 (and_3_out, ~A[1], ~A[0], B[0]);  // AND_Gate
  and and_4 (and_4_out, A[1], ~B[1]);  // AND_Gate
  and and_5 (and_5_out, A[1], A[0], ~B[0]);  // AND_Gate
  and and_6 (and_6_out, A[0], ~B[1], ~B[0]);  // AND_Gate
  or or_1 (or_1_out, ~A[1], B[1]);  // OR_Gate
  or or_2 (or_2_out, A[0], ~B[0]);  // OR_Gate
  or or_3 (LT, and_1_out, and_2_out, and_3_out);
  or or_4 (GT, and_4_out, and_5_out, and_6_out);
  or or_5 (or_5_out, A[1], ~B[1]);  // OR_Gate
  or or_6 (or_6_out, ~A[0], B[0]);  // OR_Gate
  and and_7 (EQ, or_1_out, or_2_out, or_5_out, or_6_out);

  // Notes on the sheet:
  //   2-bit Comparator - Output if A is LT, EQ, or GT B
endmodule

module _4_bit_Comparator__good (
  input  [3:0] X,
  input  [3:0] Y,
  output LT,
  output EQ,
  output GT
);

  wire n1_bit_comparator_rev_1_eq_2, n1_bit_comparator_rev_1_gt_2, n1_bit_comparator_rev_1_lt_2,
       n1_bit_comparator_rev_2_eq_2, n1_bit_comparator_rev_2_gt_2, n1_bit_comparator_rev_2_lt_2,
       n1_bit_comparator_rev_3_eq_2, n1_bit_comparator_rev_3_gt_2, n1_bit_comparator_rev_3_lt_2;

  _1_bit_Comparator__rev u_1_bit_comparator_rev_1 (
    .LT(n1_bit_comparator_rev_2_lt_2), .EQ(n1_bit_comparator_rev_2_eq_2), .GT(n1_bit_comparator_rev_2_gt_2),
    .X(X[2]), .Y(Y[2]), .LT_2(n1_bit_comparator_rev_1_lt_2), .EQ_2(n1_bit_comparator_rev_1_eq_2),
    .GT_2(n1_bit_comparator_rev_1_gt_2));
  _1_bit_Comparator__rev u_1_bit_comparator_rev_2 (
    .LT(1'b0), .EQ(1'b1), .GT(1'b0), .X(X[3]), .Y(Y[3]), .LT_2(n1_bit_comparator_rev_2_lt_2),
    .EQ_2(n1_bit_comparator_rev_2_eq_2), .GT_2(n1_bit_comparator_rev_2_gt_2));
  _1_bit_Comparator__rev u_1_bit_comparator_rev_3 (
    .LT(n1_bit_comparator_rev_1_lt_2), .EQ(n1_bit_comparator_rev_1_eq_2), .GT(n1_bit_comparator_rev_1_gt_2),
    .X(X[1]), .Y(Y[1]), .LT_2(n1_bit_comparator_rev_3_lt_2), .EQ_2(n1_bit_comparator_rev_3_eq_2),
    .GT_2(n1_bit_comparator_rev_3_gt_2));
  _1_bit_Comparator__rev u_1_bit_comparator_rev_4 (
    .LT(n1_bit_comparator_rev_3_lt_2), .EQ(n1_bit_comparator_rev_3_eq_2), .GT(n1_bit_comparator_rev_3_gt_2),
    .X(X[0]), .Y(Y[0]), .LT_2(LT), .EQ_2(EQ), .GT_2(GT));

  // Notes on the sheet:
  //   4-bit Comparator - Use 4x 1-bit Comp.
endmodule

module _2x1_MUX (
  input  A,
  input  A_2,
  input  B,
  input  B_2,
  input  S,
  input  S_2,
  output Out,
  output Out_2
);

  wire and_1_out, and_2_out;

  and and_1 (and_1_out, A, ~S_2);  // AND_Gate
  and and_2 (and_2_out, B, S_2);
  or or_1 (Out, and_1_out, and_2_out);
  Multiplexer #(.enable("false")) multiplexer_1 (.in0(A_2), .in1(B_2), .out(Out_2), .sel(S));

  // Notes on the sheet:
  //   2x1 Multiplexer - Output A if S = 0, otherwise B
endmodule

module _4x1_MUX (
  input  A,
  input  B,
  input  C,
  input  D,
  input  S1,
  input  S0,
  output Out
);

  wire and_1_out, and_2_out, and_3_out, and_4_out;

  and and_1 (and_1_out, A, ~S1, ~S0);  // AND_Gate
  and and_2 (and_2_out, B, ~S1, S0);  // AND_Gate
  and and_3 (and_3_out, C, S1, ~S0);  // AND_Gate
  and and_4 (and_4_out, D, S1, S0);
  or or_1 (Out, and_1_out, and_2_out, and_3_out, and_4_out);

  // Notes on the sheet:
  //   4x1 Multiplexer - Choose output from A, B, C, or D
endmodule

module _4x1_w__2x1_MUX (
  input  A,
  input  B,
  input  C,
  input  D,
  input  S1,
  input  S0,
  output Out
);

  wire multiplexer_1_out, multiplexer_2_out;

  Multiplexer #(.enable("false")) multiplexer_1 (.in0(A), .in1(B), .out(multiplexer_1_out), .sel(S0));
  Multiplexer #(.enable("false")) multiplexer_2 (.in0(C), .in1(D), .out(multiplexer_2_out), .sel(S0));
  Multiplexer #(.enable("false")) multiplexer_3 (.in0(multiplexer_1_out), .in1(multiplexer_2_out), .out(Out), .sel(S1));

  // Notes on the sheet:
  //   4x1 Multiplexer - Built with smaller MUX
endmodule

module _8x1_MUX_as_Comb (
  input  A,
  input  B,
  input  C,
  output Out
);

  Multiplexer #(.select(3), .enable("false")) multiplexer_1 (
    .in0(1'b0), .in1(1'b1), .in2(1'b0), .in3(1'b0), .in4(1'b1), .in5(1'b1), .in6(1'b0), .in7(1'b1),
    .out(Out), .sel({A, B, C}));

  // Notes on the sheet:
  //   8x1 Multiplexer - Build any 3-input combinational circuit
  //   Truth Table Outputs:
  //   0
  //   1
  //   0
  //   0
  //   1
  //   1
  //   0
  //   1
endmodule

module _8x1_w__other_MUX (
  input  [3:0] A,
  input  [3:0] B,
  input  [3:0] C,
  input  [3:0] D,
  input  [3:0] E,
  input  [3:0] F,
  input  [3:0] G,
  input  [3:0] H,
  input  S2,
  input  S1,
  input  S0,
  output [3:0] Out
);

  wire [3:0] multiplexer_1_out, multiplexer_2_out;

  Multiplexer #(.select(2), .width(4), .enable("false")) multiplexer_1 (
    .in0(A), .in1(B), .in2(C), .in3(D), .out(multiplexer_1_out), .sel({S1, S0}));
  Multiplexer #(.select(2), .width(4), .enable("false")) multiplexer_2 (
    .in0(E), .in1(F), .in2(G), .in3(H), .out(multiplexer_2_out), .sel({S1, S0}));
  Multiplexer #(.width(4), .enable("false")) multiplexer_3 (
    .in0(multiplexer_1_out), .in1(multiplexer_2_out), .out(Out), .sel(S2));

  // Notes on the sheet:
  //   8x1 Multiplexer - with other Multiplexers
endmodule

module _2x4_Decoder (
  input  S1,
  input  S1_2,
  input  S0,
  input  S0_2,
  input  Enable,
  input  Enable_2,
  output D0,
  output D0_2,
  output D1,
  output D1_2,
  output D2,
  output D2_2,
  output D3,
  output D3_2
);

  and and_1 (D0, ~S1, ~S0, Enable);  // AND_Gate
  and and_2 (D1, ~S1, S0, Enable);  // AND_Gate
  and and_3 (D2, S1, ~S0, Enable);  // AND_Gate
  and and_4 (D3, S1, S0, Enable);
  Decoder #(.select(2), .disabled(0)) decoder_1 (
    .out0(D0_2), .out1(D1_2), .out2(D2_2), .out3(D3_2), .sel({S1_2, S0_2}), .en(Enable_2));

  // Notes on the sheet:
  //   2x4 Decoder - Enable the indicated output
endmodule

module _3x8_Decoder_as_Comb (
  input  A,
  input  B,
  input  C,
  output Out
);

  wire decoder_1_out1, decoder_1_out4, decoder_1_out5, decoder_1_out7;

  Decoder #(.select(3), .enable("false")) decoder_1 (
    .out1(decoder_1_out1), .out4(decoder_1_out4), .out5(decoder_1_out5), .out7(decoder_1_out7),
    .sel({A, B, C}));  // open: out0, out2, out3, out6
  or or_1 (Out, decoder_1_out1, decoder_1_out7, decoder_1_out4, decoder_1_out5);

  // Notes on the sheet:
  //   3x8 Decoder - Build any 3-input combinational circuit
  //   Truth Table Outputs:
  //   0
  //   1
  //   0
  //   0
  //   1
  //   1
  //   0
  //   1
endmodule
