// Logisim project custom_reg.circ as structural Verilog: 12 circuits, main circuit Register
module _1bit_reg (
  input  Clock,
  input  Data,
  input  Load,
  input  Clear,
  output Data_out
);

  wire and_1_out, and_2_out;

  and and_1 (and_1_out, Load, Data);
  and and_2 (and_2_out, Load, ~Data);  // AND_Gate
  J_K_Flip_Flop j_k_ff_1 (
    .J(and_1_out), .clk(Clock), .K(and_2_out), .Q(Data_out), .reset(Clear));  // open: Qn, preset, en

  // Notes on the sheet:
  //   Jaylon Atkins
  //   OLA 5
  //   1bit_reg
endmodule

// Reg
module Register (
  input  Clock,
  input  [31:0] Data_In,
  input  Load,
  output [31:0] Data_out
);

  Register_part #(.width(32)) register_1 (.D(Data_In), .en(Load), .Q(Data_out), .clk(Clock), .clr(1'b0));

  // Notes on the sheet:
  //   Jaylon Atkins
  //   OLA 5
  //   Register
endmodule

// Bus
module BusRegister (
  input  Clock,
  input  [31:0] Data_In,
  input  Load,
  input  Bus,
  output [31:0] Data_out,
  output [31:0] Bus_out
);

  Register_part #(.width(32)) register_1 (.D(Data_In), .en(Load), .Q(Data_out), .clk(Clock), .clr(Clock));
  assign Bus_out = Bus ? Data_out : 32'bz;  // Controlled_Buffer controlled_buffer_1
  // also tied to GND on the sheet: Clock

  // Notes on the sheet:
  //   Jaylon Atkins
  //   OLA 5
  //   Bus Register
endmodule

// Clear
module ClearRegister (
  input  Clock,
  input  [31:0] Data_In,
  input  Load,
  input  Clear,
  input  Bus,
  output [31:0] Data_out,
  output [31:0] Bus_out
);

  Register_part #(.width(32)) register_1 (.D(Data_In), .en(Load), .Q(Data_out), .clk(Clock), .clr(Clear));
  assign Bus_out = Bus ? ~Data_In : 32'bz;  // Controlled_Inverter controlled_inverter_1

  // Notes on the sheet:
  //   Jaylon Atkins
  //   OLA 5
  //   Clear Register
endmodule

// Count
module CountRegister (
  input  Clock,
  input  [31:0] Data_In,
  input  Bus,
  input  Count,
  input  Load,
  output [31:0] Data_Out,
  output [31:0] Bus_Out
);

  wire or_1_out;
  wire [31:0] adder_1_out, multiplexer_1_out;

  Multiplexer #(.width(32), .enable("false")) multiplexer_1 (
    .in0(Data_In), .in1(adder_1_out), .out(multiplexer_1_out), .sel(Count));
  Adder #(.width(32)) adder_1 (.a(Data_Out), .b(32'h1), .out(adder_1_out));  // open: cin, cout
  BusRegister busregister_1 (
    .Data_In(multiplexer_1_out), .Clock(Clock), .Load(or_1_out), .Bus(Bus), .Data_out(Data_Out),
    .Bus_out(Bus_Out));
  or or_1 (or_1_out, Count, Load);

  // Notes on the sheet:
  //   Jaylon Atkins
  //   OLA 5
  //   Count Register
endmodule

module ACC (
  input  Clock,
  input  [31:0] Data_In,
  input  Load,
  input  Clear,
  input  Bus,
  output [31:0] Data_Out,
  output [31:0] Bus_out
);

  ClearRegister clearregister_1 (
    .Data_In(Data_In), .Clock(Clock), .Load(Load), .Clear(Clear), .Bus(Bus), .Data_out(Data_Out),
    .Bus_out(Bus_out));

  // Notes on the sheet:
  //   Jaylon Atkins
  //   OLA 5
  //   Accumulator
endmodule

module AR (
  input  Clock,
  input  [31:0] Data_In,
  input  Load,
  output [31:0] Data_out
);

  Register register_1 (.Data_In(Data_In), .Clock(Clock), .Load(Load), .Data_out(Data_out));

  // Notes on the sheet:
  //   Jaylon Atkins
  //   OLA 5
  //   Address Register
endmodule

module DR (
  input  Clock,
  input  [31:0] Data_In,
  input  Load,
  input  Bus,
  output [31:0] Data_Out,
  output [31:0] Bus_out
);

  BusRegister busregister_1 (
    .Data_In(Data_In), .Clock(Clock), .Load(Load), .Bus(Bus), .Data_out(Data_Out), .Bus_out(Bus_out));

  // Notes on the sheet:
  //   Jaylon Atkins
  //   OLA 5
  //   Data Register
endmodule

module IR (
  input  Clock,
  input  [31:0] Data_In,
  input  Load,
  output [31:0] Data_out
);

  Register register_1 (.Data_In(Data_In), .Clock(Clock), .Load(Load), .Data_out(Data_out));

  // Notes on the sheet:
  //   Jaylon Atkins
  //   OLA 5
  //   Instruction Register
endmodule

module OUTR (
  input  Clock,
  input  [31:0] Data_In,
  input  Load,
  output [31:0] Data_out
);

  Register register_1 (.Data_In(Data_In), .Clock(Clock), .Load(Load), .Data_out(Data_out));

  // Notes on the sheet:
  //   Jaylon Atkins
  //   OLA 5
  //   Output Register
endmodule

module PC (
  input  Clock,
  input  [31:0] Data_In,
  input  Load,
  input  Count,
  input  Bus,
  output [31:0] Data_Out,
  output [31:0] Bus_out
);

  CountRegister countregister_1 (
    .Data_In(Data_In), .Clock(Clock), .Count(Load), .Load(Count), .Bus(Bus), .Data_Out(Data_Out),
    .Bus_Out(Bus_out));

  // Notes on the sheet:
  //   Jaylon Atkins
  //   OLA 5
  //   Program Counter
endmodule

module R (
  input  Clock,
  input  [31:0] Data_In,
  input  Load,
  input  Bus,
  output [31:0] Data_Out,
  output [31:0] Bus_out
);

  BusRegister busregister_1 (
    .Data_In(Data_In), .Clock(Clock), .Load(Load), .Bus(Bus), .Data_out(Data_Out), .Bus_out(Bus_out));
endmodule
