// Logisim project initial_labs.circ as structural Verilog: 3 circuits, main circuit x3plus6
module x3plus6 (
  input  A,
  input  B,
  output W_A_B,
  output X_A_B,
  output Y_A_B,
  output Z_A_B
);

  wire AND_out;

  or OR (W_A_B, B, A);
  and AND (AND_out, A, B);
  xnor XNOR (Y_A_B, B, A);
  buf buffer_1 (Z_A_B, B);
  xnor xnor_2 (X_A_B, AND_out, B);

  // Notes on the sheet:
  //   Jaylon Atkins
  //   CLA 1
  //   x3plus6
endmodule

module generator (
  input  [2:0] C,
  output [3:0] X
);

  wire XOR_out;

  xor XOR (XOR_out, C[0], C[0]);
  xor XOR_2 (X[0], XOR_out, C[2]);

  assign X[3:1] = C;

  // Notes on the sheet:
  //   Jaylon Atkins
  //   Generator
  //   A
  //   B
  //   Y
  //   Z
  //   P
endmodule

module \checker  (
  input  [3:0] in_1,
  output Checker
);

  wire XOR_2_out, XOR_out;

  xor XOR (XOR_out, in_1[0], in_1[1]);
  xor XOR_2 (XOR_2_out, in_1[2], in_1[3]);
  xor XOR_3 (Checker, XOR_out, XOR_2_out);

  // Notes on the sheet:
  //   Jaylon Atkins
  //   Checker
  //   D
  //   B
  //   C
  //   A
endmodule
