// Logisim project mod_counter.circ as structural Verilog: 2 circuits, main circuit Mod9
module Mod9 (
  input  Clock,
  output [3:0] Output
);

  wire AND_2_out, AND_3_out, AND_out, not_1_out, not_2_out, not_3_out, not_4_out, not_5_out, not_6_out,
       not_7_out, OR_out;

  not not_1 (not_1_out, Output[2]);
  not not_2 (not_2_out, Output[1]);
  not not_3 (not_3_out, Output[0]);
  not not_4 (not_4_out, Output[2]);
  and AND (AND_out, not_1_out, Output[0], Output[1]);
  or OR (OR_out, not_2_out, not_3_out);
  not not_5 (not_5_out, Output[3]);
  and AND_2 (AND_2_out, not_5_out, not_4_out, Output[0]);
  not not_6 (not_6_out, Output[3]);
  not not_7 (not_7_out, Output[2]);
  and AND_3 (AND_3_out, not_6_out, not_7_out);
  J_K_Flip_Flop A (.J(AND_out), .clk(Clock), .K(1'b1), .Q(Output[3]), .en(1'b1));  // open: Qn, preset, reset
  J_K_Flip_Flop B (.J(OR_out), .clk(Clock), .K(1'b1), .Q(Output[2]));  // open: Qn, preset, en, reset
  J_K_Flip_Flop C (.J(AND_2_out), .clk(Clock), .K(AND_2_out), .Q(Output[1]), .en(1'b1));  // open: Qn, preset, reset
  J_K_Flip_Flop D (.J(AND_3_out), .clk(Clock), .K(not_7_out), .Q(Output[0]), .en(1'b1));  // open: Qn, preset, reset
endmodule

module Display (
);

  wire clock_1_out, n7segdecoder_1_a, n7segdecoder_1_b, n7segdecoder_1_c, n7segdecoder_1_d, n7segdecoder_1_e,
       n7segdecoder_1_f, n7segdecoder_1_g;
  wire [3:0] mod9_1_output;

  Clock clock_1 (.out(clock_1_out));
  Mod9 mod9_1 (.Clock(clock_1_out), .Output(mod9_1_output));
  _7SegDecoder u_7segdecoder_1 (
    .BCD_In(mod9_1_output), .a(n7segdecoder_1_a), .b(n7segdecoder_1_b), .c(n7segdecoder_1_c),
    .d(n7segdecoder_1_d), .e(n7segdecoder_1_e), .f(n7segdecoder_1_f), .g(n7segdecoder_1_g));  // open: DP_In, DP_Out
  _7_Segment_Display u_7_segment_display_1 (
    .g(n7segdecoder_1_g), .f(n7segdecoder_1_f), .a(n7segdecoder_1_a), .b(n7segdecoder_1_b),
    .e(n7segdecoder_1_e), .d(n7segdecoder_1_d), .c(n7segdecoder_1_c));  // open: dp
endmodule
