// Logisim project rtl.circ as structural Verilog: 6 circuits, main circuit Ex. 1
module Ex__1 (
  input  Clock,
  input  A
);

  wire [3:0] Y_q;

  Register #(.width(4)) X (.D(Y_q), .en(A), .clk(Clock));  // open: Q, clr
  Register #(.width(4)) Y (.Q(Y_q), .clk(Clock));  // open: D, en, clr

  // Notes on the sheet:
  //   A: x <- y
endmodule

module Ex__2 (
  input  Clock,
  input  A
);

  wire [3:0] Y_q, Z_q;

  Register #(.width(4)) X (.D(Y_q), .en(A), .clk(Clock));  // open: Q, clr
  Register #(.width(4)) Y (.D(Z_q), .en(A), .Q(Y_q), .clk(Clock));  // open: clr
  Register #(.width(4)) Z (.Q(Z_q), .clk(Clock));  // open: D, en, clr

  // Notes on the sheet:
  //   A: x <- y, y <- z
endmodule

module Ex__3 (
  input  Clock,
  input  A,
  input  B
);

  wire or_1_out;

  or or_1 (or_1_out, A, B);
  Register #(.width(4)) X (.D({3'b000, B}), .en(or_1_out), .clk(Clock));  // open: Q, clr

  // Notes on the sheet:
  //   A: x <- 0, B: x <- 1 (A and B are mutually exclusive)
endmodule

module Ex__4 (
  input  Clock,
  input  C
);

  wire [3:0] multiplexer_1_out, Y_q, Z_q;

  Multiplexer #(.width(4), .enable("false")) multiplexer_1 (.in0(Z_q), .in1(Y_q), .out(multiplexer_1_out), .sel(C));
  Register #(.width(4)) Z (.Q(Z_q), .clk(Clock));  // open: D, en, clr
  Register #(.width(4)) X (.D(multiplexer_1_out), .en(1'b1), .clk(Clock));  // open: Q, clr
  Register #(.width(4)) Y (.Q(Y_q), .clk(Clock));  // open: D, en, clr

  // Notes on the sheet:
  //   if (C = 1) x <- y, else x <- z
  //   C: x <- y, C': x <- z
endmodule

module Ex__5__no_bus (
  input  Clock,
  input  J,
  input  O,
  input  H,
  input  N
);

  wire or_1_out;
  wire [3:0] A_q, M_q, multiplexer_1_out, R_q, Y_q;

  or or_1 (or_1_out, J, N);
  Register #(.width(4)) Y (.D(R_q), .en(N), .Q(Y_q), .clk(Clock));  // open: clr
  Multiplexer #(.width(4), .enable("false")) multiplexer_1 (.in0(A_q), .in1(R_q), .out(multiplexer_1_out), .sel(N));
  Register #(.width(4)) A (.D(Y_q), .en(O), .Q(A_q), .clk(Clock));  // open: clr
  Register #(.width(4)) M (.D(multiplexer_1_out), .en(or_1_out), .Q(M_q), .clk(Clock));  // open: clr
  Register #(.width(4)) R (.D(M_q), .en(H), .Q(R_q), .clk(Clock));  // open: clr

  // Notes on the sheet:
  //   J: M <- A
  //   O: A <- Y
  //   H: R <- M
  //   N: Y <- R, M <- R
endmodule

module Ex__5__TSB_bus (
  input  Clock,
  input  J,
  input  O,
  input  H,
  input  N
);

  wire or_1_out;
  wire [3:0] A_q, controlled_buffer_1_out, M_q, R_q, Y_q;

  or or_1 (or_1_out, J, N);
  Register #(.width(4)) M (.D(controlled_buffer_1_out), .en(or_1_out), .Q(M_q), .clk(Clock));  // open: clr
  Register #(.width(4)) A (.D(controlled_buffer_1_out), .en(O), .Q(A_q), .clk(Clock));  // open: clr
  Register #(.width(4)) R (.D(controlled_buffer_1_out), .en(H), .Q(R_q), .clk(Clock));  // open: clr
  Register #(.width(4)) Y (.D(controlled_buffer_1_out), .en(N), .Q(Y_q), .clk(Clock));  // open: clr
  assign controlled_buffer_1_out = H ? M_q : 4'bz;  // Controlled_Buffer controlled_buffer_1
  assign controlled_buffer_1_out = J ? A_q : 4'bz;  // Controlled_Buffer controlled_buffer_2
  assign controlled_buffer_1_out = N ? R_q : 4'bz;  // Controlled_Buffer controlled_buffer_3
  assign controlled_buffer_1_out = O ? Y_q : 4'bz;  // Controlled_Buffer controlled_buffer_4

  // Notes on the sheet:
  //   J: M <- A
  //   O: A <- Y
  //   H: R <- M
  //   N: Y <- R, M <- R
endmodule
